# Fritzing sketch Circuit_diagram (saved by Fritzing 1.0.5)
breadboards: 1

parts:
  U1 = LuaNode32 / ESP32 [part_number=ESP32S-PIN30]
  Part1 = Adafruit DRV8833 DC/Stepper Motor Driver [part_number="Adafruit #3297"]
  Enc1 = shaft encoder
  Enc3 = shaft encoder
  Mod1 = YL-99 Limit switch and LED
  Mod2 = YL-99 Limit switch and LED
  J1 = Basic Servo
  S1 = Round Pushbutton
  YwRobot_Power_Supply1 = YwRobot Breadboard Power Supply [part_number=545043]
  M1 = gear-motor
  M2 = gear-motor

nets:
  N1: U1.D32, Enc3.OUT
  N2: U1.D33, Enc1.OUT
  N3: U1.D25, Part1.AIN1
  N4: U1.D26, Part1.AIN2
  N5: U1.D27, Part1.BIN1
  N6: U1.D14, Part1.BIN2
  N7: U1.D12, J1.pulse
  GND: U1.GND, Part1.GND, Enc1.GND, Enc3.GND, Mod1.GND, Mod2.GND, J1.gnd, S1.leg1, YwRobot_Power_Supply1.GND
  N8: U1.D19, Mod2.OUT
  N9: U1.D21, S1.leg0
  N10: Part1.AOUT2, M1.pin_1
  N11: Part1.AOUT1, M1.pin_2
  N12: Part1.BOUT1, M2.pin_1
  N13: Part1.BOUT2, M2.pin_2
  VCC: Part1.VMOTOR, Part1.!SLEEP, Enc1.VCC, Enc3.VCC, J1.vcc, YwRobot_Power_Supply1.VCC#5
  N14: Mod2.VCC, YwRobot_Power_Supply1.VCC#9

custom parts:
  LuaNode32 / ESP32: New Image for LuaNode32 DOIT ESP32 DEVKIT V1. Base parts from LuaNode32 / ESP32 ESP32 based LuaNode32 by G.Noorlander DOIT Esp32 DevKit v1 (30 pins long, 11 pins width) by Werner Rothschopf (modified by vanepp Dec 2018)
  Adafruit DRV8833 DC/Stepper Motor Driver: Spin two DC motors or step one bi-polar or uni-polar stepper with up to 1.2A per channel using the DRV8833. This motor driver chip is a nice alternative to the TB6612 driver. Like that chip, you get 2 full H-bridges, but this chip is better for low voltage uses (can run from 2.7V up to 10.8V motor power) and has built in current limiting capability. We set it up for 1A current limiting so you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
  YwRobot Breadboard Power Supply: The YwRobot Breadboard Power Supply (MB-V2) has two power rails; they can be 5V or 3V3. Power to the module can be provided through the female USB socket or through the A10 (female) 2.1mm power jack.
